# Fritzing sketch motoryldr (saved by Fritzing 0.9.3b)
breadboards: 1

parts:
  R1 = Photocell (LDR) [package=THT]
  R2 = Resistor [tolerance=±5% resistance=10k package=THT]
  M3 = DC Motor
  Componente3 = Adafruit Motor/Stepper/Servo Shield [part_number="Adafruit #1438"]

nets:
  N1: R1.pin_0, Componente3.+5V
  N2: R1.pin_1, R2.Pin_0, Componente3.AD0
  N3: R2.Pin_1, Componente3.GND
  N4: M3.pin_1, Componente3.M1B
  N5: M3.pin_2, Componente3.M1A

custom parts:
  Adafruit Motor/Stepper/Servo Shield: The original Adafruit Motorshield kit is one of our most beloved kits, which is why we decided to make something even better. We have upgraded the shield kit to make the bestest, easiest way to drive DC and Stepper motors. This shield will make quick work of your next robotics project! We kept the ability to drive up to 4 DC motors or 2 stepper motors, but added many improvements: Instead of a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
