# Fritzing sketch rgbyboton (saved by Fritzing 0.9.3b)
breadboards: 1

parts:
  R1 = Resistor [tolerance=±5% resistance=220 package=THT]
  R2 = Resistor [tolerance=±5% resistance=220 package=THT]
  R3 = Resistor [tolerance=±5% resistance=220 package=THT]
  LED1 = RGB LED - (4 legs) [package="5 mm [THT]"]
  Componente1 = Arduino Uno (Rev3)
  S2 = Pushbutton [package="[THT]"]
  R4 = Resistor [tolerance=±5% resistance=10k package=THT]

nets:
  N1: R1.Pin_0, LED1.red_cathode
  N2: R1.Pin_1, Componente1.D13/SCK
  N3: R2.Pin_0, LED1.green_cathode
  N4: R2.Pin_1, Componente1.D12/MISO
  N5: R3.Pin_0, LED1.blue_cathode
  N6: R3.Pin_1, Componente1.D11_PWM/MOSI
  N7: LED1.common_anode, Componente1.5V, S2.Pin_3, S2.Pin_4
  N8: Componente1.D2, S2.Pin_1, S2.Pin_2, R4.Pin_0
  N9: Componente1.GND, R4.Pin_1
