# Fritzing sketch sensorproximidadyrgb (saved by Fritzing 0.9.3b)
breadboards: 1

parts:
  R1 = Resistor [tolerance=±5% resistance=220 package=THT]
  R2 = Resistor [tolerance=±5% resistance=220 package=THT]
  R3 = Resistor [tolerance=±5% resistance=220 package=THT]
  LED1 = RGB LED - (4 legs) [package="5 mm [THT]"]
  Componente1 = Arduino Uno (Rev3)
  hc-sr2 = hc-sr04

nets:
  N1: R1.Pin_0, LED1.red_cathode
  N2: R1.Pin_1, Componente1.D13/SCK
  N3: R2.Pin_0, LED1.green_cathode
  N4: R2.Pin_1, Componente1.D12/MISO
  N5: R3.Pin_0, LED1.blue_cathode
  N6: R3.Pin_1, Componente1.D11_PWM/MOSI
  5V: LED1.common_anode, Componente1.5V, hc-sr2.VCC
  N7: Componente1.D8, hc-sr2.Trig
  N8: Componente1.D7, hc-sr2.Echo
  GND: Componente1.GND, hc-sr2.GND
