# Fritzing sketch servoybotones (saved by Fritzing 0.9.3b)
breadboards: 1

parts:
  Parte1 = Arduino Uno (Rev3)
  J1 = Basic Servo
  S5 = Momentary Switch [package=ksa_sealed_tac_switch]
  S6 = Momentary Switch [package=ksa_sealed_tac_switch]
  R5 = Resistor [tolerance=±5% resistance=10k package="0603 [SMD]"]
  R6 = Resistor [tolerance=±5% resistance=10k package="0603 [SMD]"]

nets:
  N1: Parte1.D2, S5.1, R6.Pin_1
  N2: Parte1.D3_PWM, S6.1, R5.Pin_1
  5V: Parte1.5V, J1.vcc, S5.3, S6.3
  GND: Parte1.GND, J1.gnd, R5.Pin_0, R6.Pin_0
